# Fritzing sketch Project I (saved by Fritzing 0.9.3b)
breadboards: 1

parts:
  Part1 = Arduino Uno (Rev3)  # not connected
  Part2 = Arduino Motor Shield (Rev3)
  T1 = LM35 Temperature Sensor [package="TO92 [THT]"]
  M1 = DC Motor
  M2 = DC Motor
  J1 = Basic Servo
  LCD1 = LCD screen
  hc-sr1 = hc-sr04
  R1 = Trimmer Potentiometer [maximum_resistance=10kΩ package=THT]
  R2 = Resistor [tolerance=±5% resistance=220 package=THT]
  VCC1 = Battery

nets:
  VCC: Part2.5V, T1.+Vs, J1.vcc, LCD1.VDD, hc-sr1.VCC, R1.leg2, R2.Pin_0
  N1: Part2.A0, T1.Vout
  N2: Part2.D11_PWM/B, J1.pulse
  N3: Part2.D12/DirA, hc-sr1.Echo
  N4: Part2.D13/DirB, hc-sr1.Trig
  GND: Part2.GND, T1.GND, J1.gnd, LCD1.VSS, LCD1.R/W, LCD1.LED-, hc-sr1.GND, R1.leg1, VCC1.-
  N5: Part2.D2, LCD1.RS
  N6: Part2.D3_PWM/A, LCD1.E
  N7: Part2.D4, LCD1.DB4
  N8: Part2.D5_PWM, LCD1.DB5
  N9: Part2.D6_PWM, LCD1.DB6
  N10: Part2.D7, LCD1.DB7
  N11: Part2.B-, M1.pin_2
  N12: Part2.B+, M1.pin_1
  N13: Part2.A-, M2.pin_2
  N14: Part2.A+, M2.pin_1
  N15: Part2.VMOT, VCC1.+
  N16: LCD1.V0, R1.wiper
  N17: LCD1.LED+, R2.Pin_1
